# Fritzing sketch heavy_load (saved by Fritzing 0.9.3b)
breadboards: 1

parts:
  Part2 = Arduino Uno (Rev3)
  Q3 = Basic FET N-Channel [package="TO220 [THT]"]
  D1 = Rectifier Diode [part_number=1N4001 package="300 mil [THT]"]
  R1 = Resistor [tolerance=±5% resistance=10k package=THT]
  M1 = DC Motor
  VCC2 = Battery block 9V

nets:
  N1: Part2.GND, Q3.source, R1.Pin_1, VCC2.-
  N2: Part2.D3_PWM, Q3.gate, R1.Pin_0
  N3: Q3.drain, D1.anode, M1.pin_2
  N4: D1.cathode, M1.pin_1, VCC2.+
